# Fritzing sketch motorSchematic (saved by Fritzing 0.9.3b)

parts:
  Part2 = Arduino Motor Shield
  M1 = DC Motor
  M2 = DC Motor

nets:
  N1: Part2.OUT3, M1.pin_2
  N2: Part2.OUT4, M1.pin_1
  N3: Part2.OUT2, M2.pin_2
  N4: Part2.OUT1, M2.pin_1
