# Fritzing sketch testSensorSchematic (saved by Fritzing 0.9.3b)
breadboards: 1

parts:
  Part1 = Arduino Uno (Rev3) - ICSP
  LED1 = LEDs [package=led10mm]
  LED2 = LEDs [package=led10mm]
  Part2 = MyoWare Cable Shield
  Part3 = MyoWare Cable Shield
  R1 = Resistor [tolerance=±5% resistance=220 package="2010 [SMD]"]
  R2 = Resistor [tolerance=±5% resistance=220 package="2010 [SMD]"]

nets:
  N1: Part1.A0, Part2.SIG
  N2: Part1.A3, Part3.SIG
  N3: Part1.D9_PWM, R2.Pin_0
  N4: Part1.D11_PWM/MOSI, R1.Pin_0
  VCC: Part1.5V, Part2.VCC, Part3.VCC
  GND: Part1.GND, LED1.A, LED2.A, Part2.GND, Part3.GND
  N5: LED1.C, R2.Pin_1
  N6: LED2.C, R1.Pin_1
